// Logisim project LC-3final.circ as structural Verilog: 29 circuits, main circuit main
module main (
  input  Reset,
  output out_2,
  output out_3,
  output out_4,
  output out_5,
  output out_6,
  output out_7,
  output out_8,
  output [15:0] out_9,
  output [15:0] out_10,
  output [15:0] out_11,
  output [15:0] out_12,
  output [15:0] out_13,
  output [15:0] out_14,
  output [15:0] out_15,
  output [15:0] out_16,
  output [15:0] out_17,
  output halt,
  output [15:0] out_19,
  output [15:0] out_20,
  output [15:0] out_21,
  output [15:0] out_22
);

  wire and_2_out, decodeir_1_ldi_sti, decodeir_1_writereg, Exec2, Fetch2, getcst_1_usecst, JSR_R,
       or16_1_out_2, or16_2_out_2, ramctrl_1_memload, ramctrl_1_memstore;
  wire [2:0] nzp_1_nzp;
  wire [15:0] alu_1_output, getcst_1_cst, LoadRes, RegIN, registres_1_out_sr1, registres_1_out_sr2,
       regpc_1_jsr_r, SR;

  BiClock biclock_1 (.reset(Reset), .Fetch1(out_2), .Exec1(out_3), .Fetch2(Fetch2), .Exec2(Exec2));
  RegPC regpc_1 (
    .H(out_3), .PC(out_9), .Reset(Reset), .IR(out_10), .R(registres_1_out_sr1), .TestNZP(out_5),
    .Jump(out_4), .JSR_R(regpc_1_jsr_r));
  // Probe on out_9
  GetAddr getaddr_1 (
    .PC(out_9), .R(registres_1_out_sr1), .IR(out_10), .Addr(out_11), .Fetch(out_2), .MemOut(out_13),
    .Fetch2(Fetch2));
  // Probe on out_11
  // Probe on out_12
  RAM #(.addrWidth(16), .dataWidth(16), .bus("separate")) ram_1 (
    .addr(out_11), .din(out_12), .data(out_13), .str(ramctrl_1_memstore), .clk(ramctrl_1_memstore),
    .ld(ramctrl_1_memload));  // open: sel, clr
  LED led_1 (.in(out_6));
  RamCtrl ramctrl_1 (
    .Store(out_7), .Fetch1(out_2), .Exec1(out_3), .Load(out_6), .MemStore(ramctrl_1_memstore),
    .MemLoad(ramctrl_1_memload), .Exec2(Exec2), .Fetch2(Fetch2), .LDI__STI(decodeir_1_ldi_sti));
  LED led_2 (.in(out_7));
  MemIn memin_1 (.SR(SR), .IR(out_10), .MemIn(out_12));
  // Probe on out_13
  DecodeIR decodeir_1 (
    .IR(out_10), .Jump(out_4), .WriteReg(decodeir_1_writereg), .Load(out_6), .Store(out_7), .JSR_R(JSR_R),
    .LDI_STI(decodeir_1_ldi_sti));
  LOAD load_1 (.IR(out_10), .PC(out_9), .DR(LoadRes), .MemOut(out_13));
  Register #(.width(16), .trigger("falling")) RegIR (.D(out_13), .Q(out_10), .clk(out_2));  // open: en, clr
  // Probe on out_10[11:9]
  // Probe on out_10[8:6]
  // Probe on out_10[2:0]
  ALU alu_1 (
    .UseCst(getcst_1_usecst), .e2(out_10[15:14]), .Input1(registres_1_out_sr1), .Input2(registres_1_out_sr2),
    .Cst(getcst_1_cst), .Output(alu_1_output), .Reset_Set(out_10[4]));
  // Probe on getcst_1_cst
  GetCst getcst_1 (.IR(out_10), .Cst(getcst_1_cst), .UseCst(getcst_1_usecst));
  // Probe on out_10[15:14]
  and and_1 (out_8, decodeir_1_writereg, out_3);
  RegCtrlIn regctrlin_1 (
    .JSR_R(regpc_1_jsr_r), .ALUOut(alu_1_output), .LEA_LD_LDR_LDI(LoadRes), .IR(out_10), .RegIN(RegIN));
  and and_2 (and_2_out, JSR_R, out_3);
  Registres registres_1 (
    .SR1(out_10[8:6]), .IN(RegIN), .SR2(out_10[2:0]), .WriteReg(out_8), .DR_SR(out_10[11:9]),
    .OUT_SR1(registres_1_out_sr1), .OUT_SR2(registres_1_out_sr2), .OUT_SR(SR), .R0(out_14), .R1(out_15),
    .R2(out_16), .R3(out_17), .R4(out_19), .R5(out_20), .R6(out_21), .R7(out_22), .JSR_R(and_2_out));
  // Probe on registres_1_out_sr2
  // Probe on registres_1_out_sr1
  // Probe on alu_1_output
  NZP nzp_1 (.NZP(nzp_1_nzp), .IR(out_10), .TestNZP(out_5), .WriteReg(out_8), .AluRES(alu_1_output), .LoadRES(LoadRes));
  // Probe on nzp_1_nzp
  Or16 or16_1 (.in_1(out_10), .out_2(or16_1_out_2));
  and and_3 (halt, ~or16_1_out_2, or16_2_out_2);  // AND_Gate
  Or16 or16_2 (.in_1(out_9), .out_2(or16_2_out_2));
  // Probe on out_14
  // Probe on out_15
  // Probe on out_16
  // Probe on out_17
  // Probe on out_19
  // Probe on out_20
  // Probe on out_21
  // Probe on out_22

  // Other names for the same wires on the sheet: Addr[15:0] = out_11; Condition = out_5; Exec = out_3; Fetch = out_2;
  //   IR[15:0] = out_10; JumpInstr = out_4; Load = out_6; MemIN[15:0] = out_12; MemOUT[15:0] = out_13;
  //   PC[15:0] = out_9; R0[15:0] = out_14; R1[15:0] = out_15; R2[15:0] = out_16; R3[15:0] = out_17; R4[15:0] = out_19;
  //   R5[15:0] = out_20; R6[15:0] = out_21; R7[15:0] = out_22; Store = out_7; WriteReg = out_8

  // Notes on the sheet:
  //   PC+1
  //   R
  //   IR
  //   R
  //   IR
  //   RAM
  //   LDI/STI
  //   Traces (NE PAS MODIFIER)______________________________________________________________________________________________________
  //   GetRegs
  //   Reset/Set
  //   GetOp
  //   Arret des traces au 1er NOP
endmodule

module ALU (
  input  [15:0] Input1,
  input  [15:0] Input2,
  input  [15:0] Cst,
  input  UseCst,
  input  Reset_Set,
  input  [1:0] e2,
  output [15:0] Output
);

  wire [3:0] Input;
  wire [15:0] adder_1_out, and_1_out, and_2_out, multiplexer_3_out, not_1_out, not_2_out, or_1_out,
       rot15b_1_out, rot15b_2_out;
  wire [15:4] multiplexer_1_out;

  Multiplexer #(.width(16), .enable("false")) multiplexer_1 (
    .in0(Input2), .in1(Cst), .out({multiplexer_1_out, Input}), .sel(UseCst));
  Adder #(.width(16)) adder_1 (.a({multiplexer_1_out, Input}), .b(Input1), .out(adder_1_out));  // open: cin, cout
  assign not_1_out = ~Input1;  // NOT_Gate not_1, 16 bits wide
  assign and_1_out = Input1 & {multiplexer_1_out, Input};  // AND_Gate and_1, 16 bits wide
  Multiplexer #(.select(2), .width(16), .enable("false")) multiplexer_2 (
    .in0(adder_1_out), .in1(and_1_out), .in2(not_1_out), .in3(multiplexer_3_out), .out(Output), .sel(e2));
  Rot15b rot15b_1 (.In(16'h1), .Out(rot15b_1_out), .in_2(Input));
  assign not_2_out = ~16'h1;  // NOT_Gate not_2, 16 bits wide
  Rot15b rot15b_2 (.In(not_2_out), .Out(rot15b_2_out), .in_2(Input));
  assign or_1_out = rot15b_1_out | Input1;  // OR_Gate or_1, 16 bits wide
  assign and_2_out = Input1 & rot15b_2_out;  // AND_Gate and_2, 16 bits wide
  Multiplexer #(.width(16), .enable("false")) multiplexer_3 (
    .in0(and_2_out), .in1(or_1_out), .out(multiplexer_3_out), .sel(Reset_Set));

  // Notes on the sheet:
  //   Reset/Set
endmodule

module BiClock (
  input  reset,
  output Fetch1,
  output Fetch2,
  output Exec1,
  output Exec2
);

  wire and_1_out, horloge_out, not_1_out, register_1_q;

  Clock horloge (.out(horloge_out));
  not not_1 (not_1_out, register_1_q);
  Register #(.width(1), .trigger("falling")) register_1 (
    .D(not_1_out), .Q(register_1_q), .clk(horloge_out), .clr(reset));  // open: en
  and and_1 (and_1_out, horloge_out, ~reset);  // AND_Gate
  and and_2 (Fetch1, ~register_1_q, and_1_out);  // AND_Gate
  and and_3 (Fetch2, register_1_q, ~and_1_out);  // AND_Gate
  and and_4 (Exec1, register_1_q, and_1_out);
  and and_5 (Exec2, ~register_1_q, ~and_1_out);  // AND_Gate

  // Notes on the sheet:
  //   Ce module divise une horloge en deux sous-horloges alternées
  //   Chronogrammes :
  //   horloge: 0101010101 signal0: 0100010001 signal1: 000100010
  //   registre 1-bit
  //   Enable
  //   select : 0 / 1
endmodule

module DecodeIR (
  input  [15:0] IR,
  output Load,
  output Store,
  output WriteReg,
  output LDI_STI,
  output JSR_R,
  output Jump
);

  wire and_1_out, decoder_1_out1;

  // Probe on decoder_1_out1
  or or_1 (LDI_STI, Load, Store);
  and and_1 (and_1_out, IR[14], ~IR[15]);  // AND_Gate
  and and_2 (JSR_R, and_1_out, Jump);
  Decoder #(.select(2), .enable("false")) decoder_1 (
    .out0(Jump), .out1(decoder_1_out1), .out2(Load), .out3(Store), .sel(IR[13:12]));
  or or_2 (WriteReg, decoder_1_out1, Load);

  // Notes on the sheet:
  //   Types d'instructions
  //   Instruction modifiant les registres
endmodule

module GetAddr (
  input  [15:0] MemOut,
  input  [15:0] R,
  input  [15:0] IR,
  input  [15:0] PC,
  input  Fetch,
  input  Fetch2,
  output [15:0] Addr
);

  wire [15:0] ldst_1_addr;

  LdSt ldst_1 (.R(R), .IR(IR), .PC(PC), .Addr(ldst_1_addr), .Fetch(Fetch), .MemOut(MemOut), .Fetch2(Fetch2));
  Multiplexer #(.select(2), .width(16), .enable("false")) multiplexer_1 (
    .in0(PC), .in1(PC), .in2(ldst_1_addr), .in3(ldst_1_addr), .out(Addr), .sel(IR[13:12]));

  // Notes on the sheet:
  //   Load/Store
  //   Arith/Jmp
  //   Adresse Memoire
endmodule

module GetCst (
  input  [15:0] IR,
  output [15:0] Cst,
  output UseCst
);

  assign Cst = {{11{IR[4]}}, IR[4:0]};  // Bit_Extender bit_extender_1

  assign UseCst = IR[5];
endmodule

module NZP (
  input  [15:0] AluRES,
  input  [15:0] LoadRES,
  input  WriteReg,
  input  [15:0] IR,
  output [2:0] NZP,
  output TestNZP
);

  wire and_1_out, and_2_out, and_3_out, comparator_1_eq, comparator_1_gt, comparator_1_lt, not_1_out;
  wire [15:0] multiplexer_1_out;

  Multiplexer #(.select(2), .width(16), .enable("false")) multiplexer_1 (
    .in1(AluRES), .in2(LoadRES), .out(multiplexer_1_out), .sel(IR[13:12]));  // open: in0, in3
  Comparator #(.width(16)) comparator_1 (
    .a(multiplexer_1_out), .b({16{1'b0}}), .gt(comparator_1_gt), .eq(comparator_1_eq), .lt(comparator_1_lt));
  not not_1 (not_1_out, WriteReg);
  Register #(.width(1)) P (.D(comparator_1_gt), .Q(NZP[0]), .clk(not_1_out));  // open: en, clr
  Register #(.width(1)) Z (.D(comparator_1_eq), .Q(NZP[1]), .clk(not_1_out));  // open: en, clr
  Register #(.width(1)) N (.D(comparator_1_lt), .Q(NZP[2]), .clk(not_1_out));  // open: en, clr
  and and_1 (and_1_out, NZP[2], IR[11]);
  and and_2 (and_2_out, NZP[1], IR[10]);
  and and_3 (and_3_out, NZP[0], IR[9]);
  or or_1 (TestNZP, and_1_out, and_2_out, and_3_out);

  // Notes on the sheet:
  //   (Resultat du calcul courant)
  //   (Instruction courante)
  //   (Instruction mettant à jour NZP)
  //   Valeur actuel du registre d'état NZP
  //   Test de saut
endmodule

// Off6
module Offset6 (
  input  [15:0] IR,
  output [15:0] Off6
);

  assign Off6 = {{10{IR[5]}}, IR[5:0]};  // Bit_Extender bit_extender_1
endmodule

// Off9
module Offset9 (
  input  [15:0] IR,
  output [15:0] Off9
);

  assign Off9 = {{7{IR[8]}}, IR[8:0]};  // Bit_Extender bit_extender_1
endmodule

module Offset11 (
  input  [15:0] IR,
  output [15:0] Off11
);

  assign Off11 = {{5{IR[10]}}, IR[10:0]};  // Bit_Extender bit_extender_1
endmodule

module Or16 (
  input  [15:0] in_1,
  output out_2
);

  wire [3:0] or_1_out;

  assign or_1_out = in_1[3:0] | in_1[7:4] | in_1[11:8] | in_1[15:12];  // OR_Gate or_1, 4 bits wide
  or or_2 (out_2, or_1_out[0], or_1_out[1], or_1_out[2], or_1_out[3]);
endmodule

module RamCtrl (
  input  LDI__STI,
  input  Exec1,
  input  Fetch1,
  input  Fetch2,
  input  Load,
  input  Store,
  input  Exec2,
  output MemLoad,
  output MemStore
);

  wire and_1_out, and_2_out, and_3_out, and_4_out;

  and and_1 (and_1_out, Fetch2, LDI__STI);
  and and_2 (and_2_out, Exec1, Load);
  and and_3 (and_3_out, Exec1, ~LDI__STI, Store);  // AND_Gate
  and and_4 (and_4_out, Exec2, Store, LDI__STI);
  or or_1 (MemLoad, Fetch1, and_1_out, and_2_out);
  or or_2 (MemStore, and_3_out, and_4_out);
endmodule

module Registres (
  input  [2:0] SR1,
  input  [15:0] IN,
  input  [2:0] SR2,
  input  WriteReg,
  input  [2:0] DR_SR,
  input  JSR_R,
  output [15:0] R0,
  output [15:0] OUT_SR1,
  output [15:0] R1,
  output [15:0] R2,
  output [15:0] R3,
  output [15:0] OUT_SR2,
  output [15:0] R4,
  output [15:0] R5,
  output [15:0] OUT_SR,
  output [15:0] R6,
  output [15:0] R7
);

  wire decoder_1_out0, decoder_1_out1, decoder_1_out2, decoder_1_out3, decoder_1_out4, decoder_1_out5,
       decoder_1_out6, decoder_1_out7, or_1_out;

  Decoder #(.select(3), .disabled(0)) decoder_1 (
    .out0(decoder_1_out0), .out1(decoder_1_out1), .out2(decoder_1_out2), .out3(decoder_1_out3),
    .out4(decoder_1_out4), .out5(decoder_1_out5), .out6(decoder_1_out6), .out7(decoder_1_out7), .sel(DR_SR),
    .en(WriteReg));
  Register #(.width(16), .trigger("falling")) u_R0 (.D(IN), .Q(R0), .clk(decoder_1_out0));  // open: en, clr
  Register #(.width(16), .trigger("falling")) u_R1 (.D(IN), .Q(R1), .clk(decoder_1_out1));  // open: en, clr
  Register #(.width(16), .trigger("falling")) u_R2 (.D(IN), .Q(R2), .clk(decoder_1_out2));  // open: en, clr
  Register #(.width(16), .trigger("falling")) u_R3 (.D(IN), .Q(R3), .clk(decoder_1_out3));  // open: en, clr
  Register #(.width(16), .trigger("falling")) u_R4 (.D(IN), .Q(R4), .clk(decoder_1_out4));  // open: en, clr
  Register #(.width(16), .trigger("falling")) u_R5 (.D(IN), .Q(R5), .clk(decoder_1_out5));  // open: en, clr
  Register #(.width(16), .trigger("falling")) u_R6 (.D(IN), .Q(R6), .clk(decoder_1_out6));  // open: en, clr
  Register #(.width(16), .trigger("falling")) u_R7 (.D(IN), .Q(R7), .clk(or_1_out));  // open: en, clr
  or or_1 (or_1_out, decoder_1_out7, JSR_R);
  Multiplexer #(.select(3), .width(16), .enable("false")) multiplexer_1 (
    .in0(R0), .in1(R1), .in2(R2), .in3(R3), .in4(R4), .in5(R5), .in6(R6), .in7(R7), .out(OUT_SR1), .sel(SR1));
  Multiplexer #(.select(3), .width(16), .enable("false")) multiplexer_2 (
    .in0(R0), .in1(R1), .in2(R2), .in3(R3), .in4(R4), .in5(R5), .in6(R6), .in7(R7), .out(OUT_SR2), .sel(SR2));
  Multiplexer #(.select(3), .width(16), .enable("false")) multiplexer_3 (
    .in0(R0), .in1(R1), .in2(R2), .in3(R3), .in4(R4), .in5(R5), .in6(R6), .in7(R7), .out(OUT_SR), .sel(DR_SR));
endmodule

module RegPC (
  input  H,
  input  Reset,
  input  Jump,
  input  [15:0] IR,
  input  TestNZP,
  input  [15:0] R,
  output [15:0] PC,
  output [15:0] JSR_R
);

  wire [15:0] br_1_pc_ir_off9, jsr_r_1_pc_jsr_r, multiplexer_1_out, multiplexer_2_out, undriven;

  Adder #(.width(16)) adder_1 (.a(PC), .b({16{1'b0}}), .out(JSR_R), .cin(1'b1));  // open: cout
  Multiplexer #(.select(2), .width(16)) multiplexer_1 (
    .in0(br_1_pc_ir_off9), .in1(jsr_r_1_pc_jsr_r), .in2(undriven), .in3(R), .out(multiplexer_1_out),
    .sel(IR[15:14]), .en(Jump));
  Multiplexer #(.width(16), .enable("false")) multiplexer_2 (
    .in0(JSR_R), .in1(multiplexer_1_out), .out(multiplexer_2_out), .sel(Jump));
  JSR_R jsr_r_1 (.R(R), .PC(JSR_R), .IR(IR), .PC_JSR_R(jsr_r_1_pc_jsr_r));
  Register #(.width(16), .trigger("falling")) u_PC (.D(multiplexer_2_out), .Q(PC), .clk(H), .clr(Reset));  // open: en
  BR br_1 (.PC(JSR_R), .IR(IR), .TestNZP(TestNZP), .PC_IR_Off9(br_1_pc_ir_off9));

  // Other names for the same wires on the sheet: PC_1[15:0] = JSR_R

  // Notes on the sheet:
  //   RTI
  //   PC <- PC + 1
  //   JMP
  //   BR
endmodule

module LdSt (
  input  [15:0] R,
  input  [15:0] IR,
  input  [15:0] PC,
  input  Fetch,
  input  [15:0] MemOut,
  input  Fetch2,
  output [15:0] Addr
);

  wire [15:0] adder_1_out, adder_2_out, multiplexer_1_out, multiplexer_2_out, offset6_1_off6, offset9_1_off9,
       register_1_q, undriven;

  Offset6 offset6_1 (.IR(IR), .Off6(offset6_1_off6));
  Offset9 offset9_1 (.IR(IR), .Off9(offset9_1_off9));
  Adder #(.width(16)) adder_1 (.a(R), .b(offset6_1_off6), .out(adder_1_out));  // open: cin, cout
  Adder #(.width(16)) adder_2 (.a(offset9_1_off9), .b(PC), .out(adder_2_out), .cin(1'b1));  // open: cout
  Register #(.width(16), .trigger("falling")) register_1 (.D(MemOut), .Q(register_1_q), .clk(Fetch2));  // open: en, clr
  Multiplexer #(.width(16), .enable("false")) multiplexer_1 (
    .in0(register_1_q), .in1(adder_2_out), .out(multiplexer_1_out), .sel(Fetch2));
  Multiplexer #(.select(2), .width(16), .enable("false")) multiplexer_2 (
    .in0(adder_2_out), .in1(adder_1_out), .in2(multiplexer_1_out), .in3(undriven), .out(multiplexer_2_out),
    .sel(IR[15:14]));
  Multiplexer #(.width(16), .enable("false")) multiplexer_3 (
    .in0(multiplexer_2_out), .in1(PC), .out(Addr), .sel(Fetch));

  // Notes on the sheet:
  //   LDR/STR
  //   LD/ST
  //   TRAP
  //   LDI/STI
  //   Adresse Memoire
endmodule

module BR (
  input  [15:0] PC,
  input  [15:0] IR,
  input  TestNZP,
  output [15:0] PC_IR_Off9
);

  wire [15:0] multiplexer_1_out, offset9_1_off9;

  Offset9 offset9_1 (.IR(IR), .Off9(offset9_1_off9));
  Multiplexer #(.width(16), .enable("false")) multiplexer_1 (
    .in0({16{1'b0}}), .in1(offset9_1_off9), .out(multiplexer_1_out), .sel(TestNZP));
  Adder #(.width(16)) adder_1 (.a(PC), .b(multiplexer_1_out), .out(PC_IR_Off9));  // open: cin, cout
endmodule

module JSR_R (
  input  [15:0] R,
  input  [15:0] PC,
  input  [15:0] IR,
  output [15:0] PC_JSR_R
);

  wire [15:0] adder_1_out, offset11_1_off11;

  Offset11 offset11_1 (.IR(IR), .Off11(offset11_1_off11));
  Adder #(.width(16)) adder_1 (.a(PC), .b(offset11_1_off11), .out(adder_1_out));  // open: cin, cout
  Multiplexer #(.width(16), .enable("false")) multiplexer_1 (.in0(R), .in1(adder_1_out), .out(PC_JSR_R), .sel(IR[11]));

  // Notes on the sheet:
  //   JSRR
  //   JSR
endmodule

module MemIn (
  input  [15:0] SR,
  input  [15:0] IR,
  output [15:0] MemIn
);

  wire [15:0] undriven;

  Multiplexer #(.select(2), .width(16), .enable("false")) multiplexer_1 (
    .in0(SR), .in1(SR), .in2(SR), .in3(undriven), .out(MemIn), .sel(IR[15:14]));

  // Notes on the sheet:
  //   ST
  //   STR
  //   STI
  //   TRAP
endmodule

module LOAD (
  input  [15:0] IR,
  input  [15:0] PC,
  input  [15:0] MemOut,
  output [15:0] DR
);

  wire [15:0] adder_1_out, offset9_1_off9;

  Offset9 offset9_1 (.IR(IR), .Off9(offset9_1_off9));
  Adder #(.width(16)) adder_1 (.a(offset9_1_off9), .b(PC), .out(adder_1_out), .cin(1'b1));  // open: cout
  Multiplexer #(.select(2), .width(16), .enable("false")) multiplexer_1 (
    .in0(MemOut), .in1(MemOut), .in2(MemOut), .in3(adder_1_out), .out(DR), .sel(IR[15:14]));

  // Notes on the sheet:
  //   LEA
  //   LD/LDR/LDI
endmodule

module RegCtrlIn (
  input  [15:0] JSR_R,
  input  [15:0] ALUOut,
  input  [15:0] LEA_LD_LDR_LDI,
  input  [15:0] IR,
  output [15:0] RegIN
);

  Multiplexer #(.select(2), .width(16), .enable("false")) multiplexer_1 (
    .in0(JSR_R), .in1(ALUOut), .in2(LEA_LD_LDR_LDI), .out(RegIN), .sel(IR[13:12]));  // open: in3
endmodule

module ResNZP (
  input  [15:0] AluRes,
  input  [15:0] LoadRes,
  input  [15:0] IR,
  output [15:0] ResNZP
);

  Multiplexer #(.select(2), .width(16), .enable("false")) multiplexer_1 (
    .in1(AluRes), .in2(LoadRes), .out(ResNZP), .sel(IR[13:12]));  // open: in0, in3
endmodule

module Rot1 (
  input  [15:0] In,
  input  e,
  output [15:0] Out
);

  Multiplexer #(.width(16), .enable("false")) multiplexer_1 (.in0(In), .in1({In[14:0], In[15]}), .out(Out), .sel(e));
endmodule

module Rot2b (
  input  [15:0] In,
  input  e,
  output [15:0] Out
);

  Multiplexer #(.width(16), .enable("false")) multiplexer_1 (.in0(In), .in1({In[13:0], In[15:14]}), .out(Out), .sel(e));
endmodule

module Rot3b (
  input  [15:0] In,
  input  [1:0] e,
  output [15:0] Out
);

  wire [15:0] rot1_1_out;

  Rot1 rot1_1 (.In(In), .e(e[0]), .Out(rot1_1_out));
  Rot2b rot2b_1 (.In(rot1_1_out), .e(e[1]), .Out(Out));
endmodule

module Rot4b (
  input  [15:0] In,
  output [15:0] Out
);


  assign Out = {In[11:0], In[15:12]};
endmodule

module Rot12b (
  input  [15:0] In,
  input  [1:0] e,
  output [15:0] Out
);

  wire [15:0] rot4b_1_out, rot4b_2_out, rot4b_3_out;

  Rot4b rot4b_1 (.In(In), .Out(rot4b_1_out));
  Rot4b rot4b_2 (.In(rot4b_1_out), .Out(rot4b_2_out));
  Rot4b rot4b_3 (.In(rot4b_2_out), .Out(rot4b_3_out));
  Multiplexer #(.select(2), .width(16), .enable("false")) multiplexer_1 (
    .in0(In), .in1(rot4b_1_out), .in2(rot4b_2_out), .in3(rot4b_3_out), .out(Out), .sel(e));
endmodule

module Rot15b (
  input  [15:0] In,
  input  [3:0] in_2,
  output [15:0] Out
);

  wire [15:0] rot3b_1_out;

  Rot3b rot3b_1 (.In(In), .Out(rot3b_1_out), .e(in_2[1:0]));
  Rot12b rot12b_1 (.In(rot3b_1_out), .Out(Out), .e(in_2[3:2]));
endmodule

module Reset (
  input  [15:0] In,
  input  in_2,
  input  in_3,
  output [15:0] Out,
  output out_5
);

  xor xor_1 (out_5, in_2, in_3);
endmodule

module Alu2 (
  input  [15:0] Input1,
  input  [15:0] Input2,
  input  [15:0] Cst,
  input  UseCst,
  input  Reset_Set,
  input  [1:0] e2,
  output [15:0] Output
);

  wire Null;
  wire [15:0] adder_1_out, and_1_out, multiplexer_1_out, multiplexer_3_out, multiplexer_4_out, not_1_out,
       or_1_out, rot15b_1_out, xor_1_out;

  Multiplexer #(.width(16), .enable("false")) multiplexer_1 (
    .in0(Input2), .in1(Cst), .out(multiplexer_1_out), .sel(UseCst));
  Adder #(.width(16)) adder_1 (.a(multiplexer_1_out), .b(Input1), .out(adder_1_out));  // open: cin, cout
  Comparator #(.width(16)) comparator_1 (.a(multiplexer_1_out), .b({16{1'b0}}), .eq(Null));  // open: gt, lt
  assign not_1_out = ~Input1;  // NOT_Gate not_1, 16 bits wide
  assign and_1_out = Input1 & multiplexer_1_out;  // AND_Gate and_1, 16 bits wide
  Multiplexer #(.select(2), .width(16), .enable("false")) multiplexer_2 (
    .in0(adder_1_out), .in1(and_1_out), .in2(not_1_out), .in3(multiplexer_4_out), .out(Output), .sel(e2));
  Rot15b rot15b_1 (.In(16'h1), .Out(rot15b_1_out), .in_2(multiplexer_1_out[3:0]));
  assign xor_1_out = rot15b_1_out ^ Input1;  // XOR_Gate xor_1, 16 bits wide
  assign or_1_out = rot15b_1_out | Input1;  // OR_Gate or_1, 16 bits wide
  Multiplexer #(.width(16), .enable("false")) multiplexer_3 (
    .in0(xor_1_out), .in1(Input1), .out(multiplexer_3_out), .sel(Null));
  Multiplexer #(.width(16), .enable("false")) multiplexer_4 (
    .in0(multiplexer_3_out), .in1(or_1_out), .out(multiplexer_4_out), .sel(Reset_Set));

  // Notes on the sheet:
  //   Set/Reset
endmodule
